// Logisim project me7mendaros.circ as structural Verilog: 1 circuit, main circuit main
module main (
  input  rst,
  output [31:0] PC,
  output [31:0] ALU_OUT
);

  wire and_1_out, and_2_out, and_3_out, and_4_out, and_5_out, and_6_out, and_7_out, and_8_out, and_9_out,
       and_12_out, and_13_out, and_14_out, arithmetic, bitwise_imm, branch, clk, comparator_1_eq,
       comparator_2_eq, comparator_3_eq, comparator_4_eq, comparator_5_eq, comparator_6_eq, comparator_7_eq,
       comparator_8_eq, comparator_9_eq, comparator_10_eq, comparator_11_eq, comparator_13_eq,
       comparator_14_eq, comparator_15_eq, comparator_16_eq, comparator_17_eq, comparator_18_eq,
       comparator_19_eq, comparator_20_eq, comparator_21_eq, comparator_22_eq, comparator_23_eq,
       comparator_24_eq, comparator_25_eq, comparator_26_eq, comparator_27_eq, comparator_28_eq,
       comparator_29_eq, comparator_30_eq, comparator_31_eq, comparator_32_eq, comparator_33_eq,
       comparator_34_eq, comparator_35_eq, comparator_36_eq, comparator_37_eq, comparator_38_eq,
       comparator_39_eq, is_itype, multiplexer_1_out, multiplexer_3_out, NOP, not_1_out, not_2_out,
       not_3_out, not_4_out, not_5_out, not_6_out, or_1_out, or_2_out, or_5_out, or_8_out, or_9_out,
       or_10_out, or_11_out, or_13_out, or_14_out, or_17_out, sel_dest, sel_IorD, sel_opA, stateA, stateB,
       stateC, stateD, stateE, stateF, stateG, stateH, stateI, wr_en, wr_ir, wr_pc, zeroflag;
  wire [1:0] priority_encoder_1_out, priority_encoder_2_out;
  wire [4:0] _6_10, _11_15, _16_20, _21_25, multiplexer_7_out;
  wire [5:0] _0_5, _31_26, ALU_code, sel_alu;
  wire [31:0] A_q, alu_res, bit_extender_1_out, imm_1, imm_final, MDR_q, memory_1_p6, multiplexer_2_out,
       multiplexer_6_out, multiplexer_8_out, multiplexer_9_out, multiplexer_10_out, reg_file_1_p9,
       reg_file_1_p10, shifter_1_out, undriven, undriven_2, wr_data;

  Clock u_clk (.out(clk));
  Comparator #(.width(1)) comparator_1 (.a(stateF), .b(1'b1), .eq(comparator_1_eq));  // open: gt, lt
  // Probe on PC
  Register #(.width(32)) u_PC (.D(multiplexer_10_out), .en(wr_pc), .Q(PC), .clk(clk), .clr(rst));
  Multiplexer #(.enable("false")) multiplexer_1 (
    .in0(1'b0), .in1(1'b1), .out(multiplexer_1_out), .sel(comparator_1_eq));
  Comparator #(.width(6)) comparator_2 (.a(_31_26), .b({6{1'b0}}), .eq(comparator_2_eq));  // open: gt, lt
  Comparator #(.width(6)) comparator_3 (.a(ALU_code), .b(6'b001000), .eq(comparator_3_eq));  // open: gt, lt
  Comparator #(.width(6)) comparator_4 (.a(ALU_code), .b(6'b001010), .eq(comparator_4_eq));  // open: gt, lt
  Comparator #(.width(6)) comparator_5 (.a(ALU_code), .b(6'b001100), .eq(comparator_5_eq));  // open: gt, lt
  Comparator #(.width(6)) comparator_6 (.a(ALU_code), .b(6'b001101), .eq(comparator_6_eq));  // open: gt, lt
  Comparator #(.width(6)) comparator_7 (.a(ALU_code), .b(6'b001110), .eq(comparator_7_eq));  // open: gt, lt
  Comparator #(.width(6)) comparator_8 (.a(ALU_code), .b(6'b100011), .eq(comparator_8_eq));  // open: gt, lt
  Comparator #(.width(6)) comparator_9 (.a(ALU_code), .b(6'b101011), .eq(comparator_9_eq));  // open: gt, lt
  Comparator #(.width(6)) comparator_10 (.a(ALU_code), .b(6'b101011), .eq(comparator_10_eq));  // open: gt, lt
  Comparator #(.width(6)) comparator_11 (.a(ALU_code), .b(6'b100011), .eq(comparator_11_eq));  // open: gt, lt
  Multiplexer #(.width(32), .enable("false")) multiplexer_2 (
    .in0(PC), .in1(ALU_OUT), .out(multiplexer_2_out), .sel(sel_IorD));
  Comparator #(.width(6)) comparator_12 (.a(_31_26), .b({6{1'b0}}), .eq(sel_dest));  // open: gt, lt
  assign bit_extender_1_out = {{16{1'b0}}, {_11_15, _6_10, _0_5}};  // Bit_Extender bit_extender_1
  Multiplexer #(.enable("false")) multiplexer_3 (.in0(1'b0), .in1(stateB), .out(multiplexer_3_out), .sel(NOP));
  // Probe on multiplexer_10_out
  // Probe on memory_1_p6
  // MEMORY memory_1: pin names not known; wires that end beside it: multiplexer_2_out, wr_data, multiplexer_1_out, clk, rst, memory_1_p6
  // Probe on _31_26
  Multiplexer #(.width(32), .enable("false")) multiplexer_4 (
    .in0(imm_1), .in1(bit_extender_1_out), .out(imm_final), .sel(bitwise_imm));
  Comparator #(.width(6)) comparator_13 (.a(ALU_code), .b(6'b000100), .eq(comparator_13_eq));  // open: gt, lt
  Comparator #(.width(32)) comparator_14 (.a(undriven), .b(undriven_2), .eq(comparator_14_eq));  // open: gt, lt
  Comparator #(.width(6)) comparator_15 (.a(ALU_code), .b(6'b000101), .eq(comparator_15_eq));  // open: gt, lt
  Comparator #(.width(32)) comparator_16 (.a(alu_res), .b({32{1'b1}}), .eq(comparator_16_eq));  // open: gt, lt
  // Probe on {_31_26, _21_25, _16_20, _11_15, _6_10, _0_5}
  Register #(.width(32)) IR (
    .D(memory_1_p6), .en(wr_ir), .Q({_31_26, _21_25, _16_20, _11_15, _6_10, _0_5}), .clk(clk), .clr(rst));
  Register #(.width(32)) MDR (.D(memory_1_p6), .en(1'b1), .Q(MDR_q), .clk(clk), .clr(rst));
  or or_1 (or_1_out, stateD, stateF, stateH, stateI, multiplexer_3_out);
  or or_2 (or_2_out, comparator_8_eq, comparator_9_eq);
  buf and_1 (and_1_out, comparator_13_eq);  // AND_Gate
  buf and_2 (and_2_out, comparator_15_eq);  // AND_Gate
  Multiplexer #(.width(6), .enable("false")) multiplexer_5 (.in0(_31_26), .in1(_0_5), .out(ALU_code), .sel(sel_dest));
  Multiplexer #(.width(32), .enable("false")) multiplexer_6 (
    .in0(MDR_q), .in1(ALU_OUT), .out(multiplexer_6_out), .sel(comparator_17_eq));
  not not_1 (not_1_out, branch);
  or or_3 (arithmetic, comparator_2_eq, comparator_3_eq, comparator_4_eq, comparator_5_eq, comparator_6_eq, comparator_7_eq);
  // Probe on multiplexer_7_out
  Multiplexer #(.width(5), .enable("false")) multiplexer_7 (
    .in0(_16_20), .in1(_11_15), .out(multiplexer_7_out), .sel(sel_dest));
  // Probe on multiplexer_6_out
  Comparator #(.width(1)) comparator_17 (.a(stateD), .b(1'b1), .eq(comparator_17_eq));  // open: gt, lt
  and and_3 (and_3_out, stateB, not_1_out, arithmetic);
  and and_4 (and_4_out, stateB, or_2_out);
  and and_5 (and_5_out, stateE, comparator_10_eq);
  and and_6 (and_6_out, stateE, comparator_11_eq);
  or or_4 (branch, and_1_out, and_2_out);
  // Probe on stateA
  // Probe on stateB
  // Probe on stateC
  // Probe on stateD
  // Probe on stateE
  assign imm_1 = {{16{_11_15[4]}}, {_11_15, _6_10, _0_5}};  // Bit_Extender bit_extender_2
  // Probe on ALU_OUT
  and and_7 (and_7_out, stateB, branch);
  // Probe on stateF
  // Probe on stateG
  // Probe on stateH
  // Probe on stateI
  // Probe on reg_file_1_p9
  // REG_FILE reg_file_1: pin names not known; wires that end beside it: _21_25, _16_20, multiplexer_7_out, multiplexer_6_out, wr_en, clk, rst, imm_1, reg_file_1_p9, reg_file_1_p10, wr_data
  Shifter #(.width(32)) shifter_1 (.in(imm_final), .\dist (5'b00010), .out(shifter_1_out));
  D_Flip_Flop State_A (.clk(clk), .D(or_1_out), .Q(stateA), .preset(rst));  // open: Qn, en, reset
  D_Flip_Flop State_B (.clk(clk), .D(stateA), .Q(stateB), .reset(rst));  // open: Qn, preset, en
  D_Flip_Flop State_C (.clk(clk), .D(and_3_out), .Q(stateC), .reset(rst));  // open: Qn, preset, en
  D_Flip_Flop State_D (.clk(clk), .D(stateC), .Q(stateD), .reset(rst));  // open: Qn, preset, en
  D_Flip_Flop State_E (.clk(clk), .D(and_4_out), .Q(stateE), .reset(rst));  // open: Qn, preset, en
  D_Flip_Flop State_F (.clk(clk), .D(and_5_out), .Q(stateF), .reset(rst));  // open: Qn, preset, en
  D_Flip_Flop State_G (.clk(clk), .D(and_6_out), .Q(stateG), .reset(rst));  // open: Qn, preset, en
  D_Flip_Flop State_H (.clk(clk), .D(stateG), .Q(stateH), .reset(rst));  // open: Qn, preset, en
  Multiplexer #(.width(32), .enable("false")) multiplexer_8 (
    .in0(PC), .in1(A_q), .out(multiplexer_8_out), .sel(sel_opA));
  Register #(.width(32)) A (.D(reg_file_1_p9), .en(1'b1), .Q(A_q), .clk(clk), .clr(rst));
  Register #(.width(32)) B (.D(reg_file_1_p10), .en(1'b1), .Q(wr_data), .clk(clk), .clr(rst));
  D_Flip_Flop State_I (.clk(clk), .D(and_7_out), .Q(stateI), .reset(rst));  // open: Qn, preset, en
  Comparator #(.width(6)) comparator_18 (.a(_31_26), .b(6'b100011), .eq(comparator_18_eq));  // open: gt, lt
  Comparator #(.width(6)) comparator_19 (.a(_31_26), .b(6'b101011), .eq(comparator_19_eq));  // open: gt, lt
  Comparator #(.width(6)) comparator_20 (.a(_31_26), .b(6'b001100), .eq(comparator_20_eq));  // open: gt, lt
  Comparator #(.width(6)) comparator_21 (.a(_31_26), .b(6'b001101), .eq(comparator_21_eq));  // open: gt, lt
  Comparator #(.width(6)) comparator_22 (.a(_31_26), .b(6'b001110), .eq(comparator_22_eq));  // open: gt, lt
  Multiplexer #(.select(2), .width(32), .enable("false")) multiplexer_9 (
    .in0(wr_data), .in1(32'h4), .in2(imm_final), .in3(shifter_1_out), .out(multiplexer_9_out),
    .sel(priority_encoder_1_out));
  Comparator #(.width(6)) comparator_23 (.a(_31_26), .b({6{1'b0}}), .eq(comparator_23_eq));  // open: gt, lt
  or or_5 (or_5_out, comparator_18_eq, comparator_19_eq);
  or or_6 (bitwise_imm, comparator_20_eq, comparator_21_eq, comparator_22_eq);
  // Probe on multiplexer_8_out
  Comparator #(.width(6)) comparator_24 (.a(_31_26), .b({6{1'b0}}), .eq(comparator_24_eq));  // open: gt, lt
  not not_2 (not_2_out, comparator_23_eq);
  and and_8 (and_8_out, not_2_out, stateC);
  or or_7 (is_itype, or_5_out, bitwise_imm);
  not not_3 (not_3_out, stateI);
  and and_9 (and_9_out, comparator_24_eq, stateC);
  or or_8 (or_8_out, and_9_out, stateI);
  or or_9 (or_9_out, and_8_out, stateE);
  or or_10 (or_10_out, stateA, stateB, stateE);
  Multiplexer #(.width(32), .enable("false")) multiplexer_10 (
    .in0(ALU_OUT), .in1(alu_res), .out(multiplexer_10_out), .sel(stateA));
  // AND_Gate and_10 has open pins: in0=stateA, out=open
  // Probe on alu_res
  or or_11 (or_11_out, stateA, stateB);
  Multiplexer #(.enable("false")) multiplexer_11 (.in0(1'b0), .in1(1'b1), .out(wr_ir), .sel(comparator_25_eq));
  Comparator #(.width(1)) comparator_25 (.a(stateA), .b(1'b1), .eq(comparator_25_eq));  // open: gt, lt
  Comparator #(.width(6)) comparator_26 (.a(_31_26), .b({6{1'b0}}), .eq(comparator_26_eq));  // open: gt, lt
  not not_4 (not_4_out, comparator_26_eq);
  Comparator #(.width(6)) comparator_27 (.a(_31_26), .b({6{1'b0}}), .eq(comparator_27_eq));  // open: gt, lt
  Comparator #(.width(6)) comparator_28 (.a(ALU_code), .b(6'b000100), .eq(comparator_28_eq));  // open: gt, lt
  Comparator #(.width(6)) comparator_29 (.a(ALU_code), .b(6'b000101), .eq(comparator_29_eq));  // open: gt, lt
  // ALU alu_1: pin names not known; wires that end beside it: multiplexer_8_out, multiplexer_9_out, imm_final, _6_10, sel_alu, not_3_out, stateA, alu_res, zeroflag
  Priority_Encoder #(.select(2)) priority_encoder_1 (
    .in0(or_8_out), .in1(stateA), .in2(or_9_out), .in3(stateB), .out(priority_encoder_1_out));  // open: gs, en_out, en_in
  or or_12 (wr_en, stateD, stateH);
  or or_13 (or_13_out, stateC, stateE, stateI);
  and and_11 (sel_opA, or_13_out, not_5_out);
  not not_5 (not_5_out, or_11_out);
  Priority_Encoder #(.select(2)) priority_encoder_2 (
    .in0(not_4_out), .in1(comparator_27_eq), .in2(or_10_out), .in3(stateI), .out(priority_encoder_2_out),
    .en_in(1'b1));  // open: gs, en_out
  not not_6 (not_6_out, zeroflag);
  // Probe on ALU_OUT
  Register #(.width(32)) u_ALU_out (.D(alu_res), .en(1'b1), .Q(ALU_OUT), .clk(clk), .clr(rst));
  Multiplexer #(.select(2), .width(6), .enable("false")) multiplexer_12 (
    .in0(_31_26), .in1(_0_5), .in2(6'b100000), .in3(6'b100010), .out(sel_alu), .sel(priority_encoder_2_out));
  and and_12 (and_12_out, comparator_28_eq, zeroflag);
  and and_13 (and_13_out, comparator_29_eq, not_6_out);
  or or_14 (or_14_out, and_12_out, and_13_out);
  and and_14 (and_14_out, stateI, or_14_out);
  Comparator #(.width(6)) comparator_30 (.a(ALU_code), .b(6'b001000), .eq(comparator_30_eq));  // open: gt, lt
  Comparator #(.width(6)) comparator_31 (.a(_31_26), .b({6{1'b0}}), .eq(comparator_31_eq));  // open: gt, lt
  Comparator #(.width(6)) comparator_32 (.a(ALU_code), .b(6'b001010), .eq(comparator_32_eq));  // open: gt, lt
  Comparator #(.width(6)) comparator_33 (.a(ALU_code), .b(6'b001100), .eq(comparator_33_eq));  // open: gt, lt
  Comparator #(.width(6)) comparator_34 (.a(ALU_code), .b(6'b001101), .eq(comparator_34_eq));  // open: gt, lt
  Comparator #(.width(6)) comparator_35 (.a(ALU_code), .b(6'b001110), .eq(comparator_35_eq));  // open: gt, lt
  Comparator #(.width(6)) comparator_36 (.a(ALU_code), .b(6'b100011), .eq(comparator_36_eq));  // open: gt, lt
  Comparator #(.width(6)) comparator_37 (.a(ALU_code), .b(6'b101011), .eq(comparator_37_eq));  // open: gt, lt
  Comparator #(.width(6)) comparator_38 (.a(ALU_code), .b(6'b000100), .eq(comparator_38_eq));  // open: gt, lt
  Comparator #(.width(6)) comparator_39 (.a(ALU_code), .b(6'b000101), .eq(comparator_39_eq));  // open: gt, lt
  or or_15 (sel_IorD, stateG, stateF);
  or or_16 (wr_pc, stateA, and_14_out);
  // Probe on wr_pc
  or or_17 (or_17_out, comparator_30_eq, comparator_31_eq, comparator_32_eq, comparator_33_eq, comparator_34_eq, comparator_35_eq, comparator_36_eq, comparator_37_eq, comparator_38_eq, comparator_39_eq);
  not not_7 (NOP, or_17_out);

  // Notes on the sheet:
  //   lw
  //   sw
  //   sw
  //   lw
  //   beq
  //   bne
  //   rd
  //   sel_data
  //   ALU_Out
  //   rs
  //   Arithmetic R
  //   lw
  //   sw
  //   andi
  //   ori
  //   xori
  //   sel_opB
  //   sel_pc
  //   control signals
  //   beq
  //   bne
  //   NOP
endmodule
